// Logisim project ADDER_STAGE (1).circ as structural Verilog: 3 circuits, main circuit main
module main (
  input  [15:0] DR,
  input  [15:0] AC
);

  wire gate_structure_1_add, gate_structure_1_and, gate_structure_1_com, gate_structure_1_dr,
       gate_structure_1_inpr, gate_structure_1_load, gate_structure_1_shl, gate_structure_1_shr,
       SATGE_7_ac_i_2, STAGE_0_ac_i_2, STAGE_1_ac_i_2, STAGE_2_ac_i_2, STAGE_3_ac_i_2, STAGE_4_ac_i_2,
       STAGE_5_ac_i_2, STAGE_6_ac_i_2, STAGE_8_ac_i_2, STAGE_9_ac_i_2, STAGE_10_ac_i_2, STAGE_11_ac_i_2,
       STAGE_12_ac_i_2, STAGE_13_ac_i_2, STAGE_14_ac_i_2, STAGE_15_ac_i_2;

  gate_structure gate_structure_1 (
    .AND(gate_structure_1_and), .ADD(gate_structure_1_add), .DR(gate_structure_1_dr),
    .LOAD(gate_structure_1_load), .INPR(gate_structure_1_inpr), .COM(gate_structure_1_com),
    .SHR(gate_structure_1_shr), .SHL(gate_structure_1_shl));  // open: D0, T5, D1, D2, P, B11, R, B9, B7, B6, B5, INCREMENT, CLEAR
  stage STAGE_0 (
    .DR_i(DR[0]), .AC_i(AC[0]), .AND(gate_structure_1_and), .ADD(gate_structure_1_add),
    .DR(gate_structure_1_dr), .Load(gate_structure_1_load), .INPR(gate_structure_1_inpr),
    .COM(gate_structure_1_com), .SHR(gate_structure_1_shr), .AC_i_1(gate_structure_1_shl), .AC_i_1_2(AC[15]),
    .AC_i_2(STAGE_0_ac_i_2));  // open: INPR__bit__i, SHL, Ci, C_i_1, CLK
  stage STAGE_1 (
    .DR_i(DR[1]), .AC_i(AC[1]), .AND(gate_structure_1_and), .ADD(gate_structure_1_add),
    .DR(gate_structure_1_dr), .Load(gate_structure_1_load), .INPR(gate_structure_1_inpr),
    .COM(gate_structure_1_com), .SHR(gate_structure_1_shr), .AC_i_1(AC[2]), .SHL(gate_structure_1_shl),
    .AC_i_1_2(AC[0]), .AC_i_2(STAGE_1_ac_i_2));  // open: INPR__bit__i, Ci, C_i_1, CLK
  stage STAGE_2 (
    .DR_i(DR[2]), .AC_i(AC[2]), .AND(gate_structure_1_and), .ADD(gate_structure_1_add),
    .DR(gate_structure_1_dr), .Load(gate_structure_1_inpr), .INPR(gate_structure_1_com),
    .COM(gate_structure_1_com), .SHR(gate_structure_1_shr), .AC_i_1(AC[3]), .SHL(gate_structure_1_shl),
    .AC_i_1_2(AC[1]), .AC_i_2(STAGE_2_ac_i_2));  // open: INPR__bit__i, Ci, C_i_1, CLK
  stage STAGE_3 (
    .DR_i(DR[3]), .AC_i(AC[3]), .AND(gate_structure_1_and), .ADD(gate_structure_1_add),
    .DR(gate_structure_1_dr), .Load(gate_structure_1_load), .INPR(gate_structure_1_inpr),
    .COM(gate_structure_1_com), .SHR(gate_structure_1_shr), .AC_i_1(AC[4]), .SHL(gate_structure_1_shl),
    .AC_i_1_2(AC[2]), .AC_i_2(STAGE_3_ac_i_2));  // open: INPR__bit__i, Ci, C_i_1, CLK
  stage STAGE_4 (
    .DR_i(DR[4]), .AC_i(AC[4]), .AND(gate_structure_1_and), .ADD(gate_structure_1_add),
    .DR(gate_structure_1_dr), .Load(gate_structure_1_load), .INPR(gate_structure_1_inpr),
    .COM(gate_structure_1_com), .SHR(gate_structure_1_shr), .AC_i_1(AC[5]), .SHL(gate_structure_1_shl),
    .AC_i_1_2(AC[3]), .AC_i_2(STAGE_4_ac_i_2));  // open: INPR__bit__i, Ci, C_i_1, CLK
  stage STAGE_5 (
    .DR_i(DR[5]), .AC_i(AC[5]), .AND(gate_structure_1_and), .ADD(gate_structure_1_add),
    .DR(gate_structure_1_dr), .Load(gate_structure_1_load), .INPR(gate_structure_1_inpr),
    .COM(gate_structure_1_com), .SHR(gate_structure_1_shr), .AC_i_1(AC[6]), .SHL(gate_structure_1_shl),
    .AC_i_1_2(AC[4]), .AC_i_2(STAGE_5_ac_i_2));  // open: INPR__bit__i, Ci, C_i_1, CLK
  stage STAGE_6 (
    .DR_i(DR[6]), .AC_i(AC[6]), .AND(gate_structure_1_and), .ADD(gate_structure_1_add),
    .DR(gate_structure_1_dr), .Load(gate_structure_1_load), .INPR(gate_structure_1_inpr),
    .COM(gate_structure_1_com), .SHR(gate_structure_1_shr), .AC_i_1(AC[7]), .SHL(gate_structure_1_shl),
    .AC_i_1_2(AC[5]), .AC_i_2(STAGE_6_ac_i_2));  // open: INPR__bit__i, Ci, C_i_1, CLK
  stage SATGE_7 (
    .DR_i(DR[7]), .AC_i(AC[7]), .AND(gate_structure_1_and), .ADD(gate_structure_1_add),
    .DR(gate_structure_1_dr), .Load(gate_structure_1_load), .INPR(gate_structure_1_inpr),
    .COM(gate_structure_1_com), .SHR(gate_structure_1_shr), .AC_i_1(AC[8]), .SHL(gate_structure_1_shl),
    .AC_i_1_2(AC[6]), .AC_i_2(SATGE_7_ac_i_2));  // open: INPR__bit__i, Ci, C_i_1, CLK
  stage STAGE_8 (
    .DR_i(DR[8]), .AC_i(AC[8]), .AND(gate_structure_1_and), .ADD(gate_structure_1_add),
    .DR(gate_structure_1_dr), .Load(gate_structure_1_load), .INPR(gate_structure_1_inpr),
    .COM(gate_structure_1_com), .SHR(gate_structure_1_shr), .AC_i_1(AC[9]), .SHL(gate_structure_1_shl),
    .AC_i_1_2(AC[7]), .AC_i_2(STAGE_8_ac_i_2));  // open: INPR__bit__i, Ci, C_i_1, CLK
  stage STAGE_9 (
    .DR_i(AC[9]), .AC_i(AC[9]), .AND(gate_structure_1_and), .ADD(gate_structure_1_add),
    .DR(gate_structure_1_dr), .Load(gate_structure_1_load), .INPR(gate_structure_1_inpr),
    .COM(gate_structure_1_com), .SHR(gate_structure_1_shr), .AC_i_1(AC[10]), .SHL(gate_structure_1_shl),
    .AC_i_1_2(AC[8]), .AC_i_2(STAGE_9_ac_i_2));  // open: INPR__bit__i, Ci, C_i_1, CLK
  stage STAGE_10 (
    .DR_i(DR[10]), .AC_i(AC[10]), .AND(gate_structure_1_and), .ADD(gate_structure_1_add),
    .DR(gate_structure_1_dr), .Load(gate_structure_1_load), .INPR(gate_structure_1_inpr),
    .COM(gate_structure_1_com), .SHR(gate_structure_1_shr), .AC_i_1(AC[11]), .SHL(gate_structure_1_shl),
    .AC_i_1_2(AC[9]), .AC_i_2(STAGE_10_ac_i_2));  // open: INPR__bit__i, Ci, C_i_1, CLK
  stage STAGE_11 (
    .DR_i(DR[11]), .AC_i(AC[11]), .AND(gate_structure_1_and), .ADD(gate_structure_1_add),
    .DR(gate_structure_1_dr), .Load(gate_structure_1_load), .INPR(gate_structure_1_inpr),
    .COM(gate_structure_1_com), .SHR(gate_structure_1_shr), .AC_i_1(AC[12]), .SHL(gate_structure_1_shl),
    .AC_i_1_2(AC[10]), .AC_i_2(STAGE_11_ac_i_2));  // open: INPR__bit__i, Ci, C_i_1, CLK
  stage STAGE_12 (
    .DR_i(DR[12]), .AC_i(AC[12]), .AND(gate_structure_1_and), .ADD(gate_structure_1_add),
    .DR(gate_structure_1_dr), .Load(gate_structure_1_load), .INPR(gate_structure_1_inpr),
    .COM(gate_structure_1_com), .SHR(gate_structure_1_shr), .AC_i_1(AC[13]), .SHL(gate_structure_1_shl),
    .AC_i_1_2(AC[11]), .AC_i_2(STAGE_12_ac_i_2));  // open: INPR__bit__i, Ci, C_i_1, CLK
  stage STAGE_13 (
    .DR_i(DR[13]), .AC_i(AC[13]), .AND(gate_structure_1_and), .ADD(gate_structure_1_add),
    .DR(gate_structure_1_dr), .Load(gate_structure_1_load), .INPR(gate_structure_1_inpr),
    .COM(gate_structure_1_com), .SHR(gate_structure_1_shr), .AC_i_1(AC[14]), .SHL(gate_structure_1_shl),
    .AC_i_1_2(AC[11]), .AC_i_2(STAGE_13_ac_i_2));  // open: INPR__bit__i, Ci, C_i_1, CLK
  stage STAGE_14 (
    .DR_i(DR[14]), .AC_i(AC[14]), .AND(gate_structure_1_and), .ADD(gate_structure_1_add),
    .DR(gate_structure_1_dr), .Load(gate_structure_1_load), .INPR(gate_structure_1_inpr),
    .COM(gate_structure_1_com), .SHR(gate_structure_1_shr), .AC_i_1(AC[15]), .SHL(gate_structure_1_shl),
    .AC_i_1_2(AC[13]), .AC_i_2(STAGE_14_ac_i_2));  // open: INPR__bit__i, Ci, C_i_1, CLK
  stage STAGE_15 (
    .DR_i(DR[15]), .AC_i(AC[15]), .AND(gate_structure_1_and), .ADD(gate_structure_1_add),
    .DR(gate_structure_1_dr), .Load(gate_structure_1_load), .INPR(gate_structure_1_inpr),
    .COM(gate_structure_1_com), .SHR(gate_structure_1_shr), .SHL(gate_structure_1_shl), .AC_i_1_2(AC[14]),
    .AC_i_2(STAGE_15_ac_i_2));  // open: INPR__bit__i, AC_i_1, Ci, C_i_1, CLK

  assign DR[9] = AC[9];
endmodule

// GATE_STR
module gate_structure (
  input  D0,
  input  T5,
  input  D1,
  input  D2,
  input  P,
  input  B11,
  input  R,
  input  B9,
  input  B7,
  input  B6,
  input  B5,
  output AND,
  output ADD,
  output DR,
  output LOAD,
  output INPR,
  output COM,
  output SHR,
  output SHL,
  output INCREMENT,
  output CLEAR
);

  and and_1 (AND, D0, T5);
  and and_2 (ADD, D1, D0);
  and and_3 (DR, D2, T5);
  and and_4 (INPR, P, B11);
  and and_5 (COM, R, B9);
  and and_6 (SHR, R, B7);
  and and_7 (SHL, R, B6);
  and and_8 (INCREMENT, R, B5);
  and and_9 (CLEAR, R, B11);
  or or_1 (LOAD, AND, ADD, DR, INPR, COM, SHR, SHL);

  // Notes on the sheet:
  //   AND
  //   ADD
  //   DR
  //   INPR
  //   COM
  //   SHR
  //   SHL
  //   INC
  //   CLR
  //   LD
endmodule

// AC_STAGE
module stage (
  input  DR_i,
  input  AC_i,
  input  AND,
  input  ADD,
  input  DR,
  input  Ci,
  input  Load,
  input  INPR,
  input  INPR__bit__i,
  input  COM,
  input  CLK,
  input  SHR,
  input  AC_i_1,
  input  SHL,
  input  AC_i_1_2,
  output C_i_1,
  output AC_i_2
);

  wire adder_1_out, and_1_out, and_2_out, and_3_out, and_4_out, and_5_out, and_6_out, and_7_out, and_8_out,
       and_9_out, not_1_out, not_2_out, or_1_out;

  Adder #(.width(1)) adder_1 (.a(AC_i), .b(DR_i), .out(adder_1_out), .cin(Ci), .cout(C_i_1));
  not not_1 (not_1_out, AC_i);
  and and_1 (and_1_out, DR_i, AC_i, AND);
  and and_2 (and_2_out, ADD, adder_1_out);
  and and_3 (and_3_out, DR, DR_i);
  and and_4 (and_4_out, INPR, INPR__bit__i);
  and and_5 (and_5_out, COM, not_1_out);
  and and_6 (and_6_out, SHR, AC_i_1);
  and and_7 (and_7_out, SHL, AC_i_1_2);
  or or_1 (or_1_out, and_1_out, and_3_out, and_2_out, and_4_out, and_5_out, and_6_out, and_7_out);
  not not_2 (not_2_out, or_1_out);
  and and_8 (and_8_out, Load, or_1_out);
  and and_9 (and_9_out, not_2_out, Load);
  J_K_Flip_Flop j_k_ff_1 (.J(and_8_out), .clk(CLK), .K(and_9_out), .Q(AC_i));  // open: Qn, preset, en, reset

  assign AC_i_2 = AC_i;

  // Notes on the sheet:
  //   FA
  //   AND
  //   ADD
  //   COM
  //   SHR
  //   SHL
  //   AC(i)
endmodule
