// Logisim project Gate Structure.circ as structural Verilog: 1 circuit, main circuit main
module main (
  input  D0,
  input  T5,
  input  D1,
  input  D2,
  input  P,
  input  B11,
  input  R,
  input  B9,
  input  B7,
  input  B6,
  input  B5,
  output LD,
  output out_13,
  output out_14
);

  wire and_1_out, and_2_out, and_3_out, and_4_out, and_5_out, and_6_out, and_7_out;

  and and_1 (and_1_out, D0, T5);
  and and_2 (and_2_out, D1, D0);
  and and_3 (and_3_out, D2, T5);
  and and_4 (and_4_out, P, B11);
  and and_5 (and_5_out, R, B9);
  and and_6 (and_6_out, R, B7);
  and and_7 (and_7_out, R, B6);
  and and_8 (out_13, R, B5);
  and and_9 (out_14, R, B11);
  or or_1 (LD, and_1_out, and_2_out, and_3_out, and_4_out, and_5_out, and_6_out, and_7_out);

  // Notes on the sheet:
  //   AND
  //   ADD
  //   DR
  //   INPR
  //   COM
  //   SHR
  //   SHL
  //   INC
  //   CLR
endmodule
