// Logisim project adder stage (1).circ as structural Verilog: 3 circuits, main circuit main
module main (
  input  in_1
);

  gate_structure gate_structure_1 ();  // open: D0, T5, D1, D2, P, B11, R, B9, B7, B6, B5, AND, LD, out_14, out_15
  stage stage_1 ();  // open: DR_i, AC_i, AND, ADD, DR, Load, INPR, INPR__bit__i, COM, SHR, AC_i_1, SHL, AC_i_1_2, Ci, C_i_1, CLK, AC_i_2
endmodule

module gate_structure (
  input  D0,
  input  T5,
  input  D1,
  input  D2,
  input  P,
  input  B11,
  input  R,
  input  B9,
  input  B7,
  input  B6,
  input  B5,
  output AND,
  output LD,
  output out_14,
  output out_15
);

  wire and_2_out, and_3_out, and_4_out, and_5_out, and_6_out, and_7_out;

  and and_1 (AND, D0, T5);
  and and_2 (and_2_out, D1, D0);
  and and_3 (and_3_out, D2, T5);
  and and_4 (and_4_out, P, B11);
  and and_5 (and_5_out, R, B9);
  and and_6 (and_6_out, R, B7);
  and and_7 (and_7_out, R, B6);
  and and_8 (out_14, R, B5);
  and and_9 (out_15, R, B11);
  or or_1 (LD, AND, and_2_out, and_3_out, and_4_out, and_5_out, and_6_out, and_7_out);

  // Notes on the sheet:
  //   AND
  //   ADD
  //   DR
  //   INPR
  //   COM
  //   SHR
  //   SHL
  //   INC
  //   CLR
endmodule

// STAGE_0
module stage (
  input  DR_i,
  input  AC_i,
  input  AND,
  input  ADD,
  input  DR,
  input  Ci,
  input  Load,
  input  INPR,
  input  INPR__bit__i,
  input  COM,
  input  CLK,
  input  SHR,
  input  AC_i_1,
  input  SHL,
  input  AC_i_1_2,
  output C_i_1,
  output AC_i_2
);

  wire adder_1_out, and_1_out, and_2_out, and_3_out, and_4_out, and_5_out, and_6_out, and_7_out, and_8_out,
       and_9_out, not_1_out, not_2_out, or_1_out;

  Adder #(.width(1)) adder_1 (.a(AC_i), .b(DR_i), .out(adder_1_out), .cin(Ci), .cout(C_i_1));
  not not_1 (not_1_out, AC_i);
  and and_1 (and_1_out, DR_i, AC_i, AND);
  and and_2 (and_2_out, ADD, adder_1_out);
  and and_3 (and_3_out, DR, DR_i);
  and and_4 (and_4_out, INPR, INPR__bit__i);
  and and_5 (and_5_out, COM, not_1_out);
  and and_6 (and_6_out, SHR, AC_i_1);
  and and_7 (and_7_out, SHL, AC_i_1_2);
  or or_1 (or_1_out, and_1_out, and_3_out, and_2_out, and_4_out, and_5_out, and_6_out, and_7_out);
  not not_2 (not_2_out, or_1_out);
  and and_8 (and_8_out, Load, or_1_out);
  and and_9 (and_9_out, not_2_out, Load);
  J_K_Flip_Flop j_k_ff_1 (.J(and_8_out), .clk(CLK), .K(and_9_out), .Q(AC_i));  // open: Qn, preset, en, reset

  assign AC_i_2 = AC_i;

  // Notes on the sheet:
  //   FA
  //   AND
  //   ADD
  //   COM
  //   SHR
  //   SHL
  //   AC(i)
endmodule
