// Logisim project arithmetic_unit.circ as structural Verilog: 1 circuit, main circuit main
module main (
  input  in_1,
  input  [15:0] DATA_REGISTER,
  input  [7:0] INPUT_REGISTER,
  input  [15:0] ACCUMMULATOR
);

  wire register_1_q, undriven, undriven_2;
  wire [7:0] register_3_q;
  wire [15:0] adder_1_out, register_2_q, register_4_q;

  Register #(.width(1)) register_1 (.D(in_1), .Q(register_1_q), .clr(undriven));  // open: en, clk
  Register #(.width(16)) register_2 (.D(DATA_REGISTER), .Q(register_2_q));  // open: en, clk, clr
  Register register_3 (.D(INPUT_REGISTER), .Q(register_3_q));  // open: en, clk, clr
  Register #(.width(16)) register_4 (.D(ACCUMMULATOR), .Q(register_4_q), .clr(undriven_2));  // open: en, clk
  Adder #(.width(16)) adder_1 (.a(register_2_q), .b(register_4_q), .out(adder_1_out), .cin(1'b0), .cout(register_1_q));

  // Notes on the sheet:
  //   E FLIP FLOP
endmodule
