// Logisim project ca_computer_final.circ as structural Verilog: 14 circuits, main circuit main
module main (
  input  in_1,
  input  SC_INC,
  output [15:0] out_3
);

  wire adder_circ_1_ac_clr, adder_circ_1_ac_inc, adder_circ_1_e, clock_1_out, control_unit_1_ac_load,
       control_unit_1_ar_load, control_unit_1_b5, control_unit_1_b6, control_unit_1_b7, control_unit_1_b9,
       control_unit_1_b11, control_unit_1_d0, control_unit_1_d1, control_unit_1_d2, control_unit_1_dr_load,
       control_unit_1_ir_load, control_unit_1_mem_bus, control_unit_1_mem_load, control_unit_1_outr_load,
       control_unit_1_p, control_unit_1_pc_inc, control_unit_1_pc_load, control_unit_1_r, control_unit_1_t5,
       not_1_out;
  wire [2:0] control_unit_1_sel_bus;
  wire [15:0] adder_circ_1_ac_res, counter_1_q, counter_2_q, multiplexer_1_out, ram_1_data, register_1_q,
       register_3_q, register_4_q, register_5_q, register_6_q;

  control_unit control_unit_1 (
    .INPUT_INSTR(register_5_q), .INC_SC(SC_INC), .CLK_INPUT(clock_1_out), .D0(control_unit_1_d0),
    .D1(control_unit_1_d1), .D2(control_unit_1_d2), .T5(control_unit_1_t5), .B11(control_unit_1_b11),
    .B9(control_unit_1_b9), .B7(control_unit_1_b7), .B5(control_unit_1_b5), .B6(control_unit_1_b6),
    .MEM_BUS(control_unit_1_mem_bus), .SEL_BUS(control_unit_1_sel_bus), .R(control_unit_1_r),
    .P(control_unit_1_p), .PC_LOAD(control_unit_1_pc_load), .PC_INC(control_unit_1_pc_inc),
    .AR_LOAD(control_unit_1_ar_load), .AC_LOAD(control_unit_1_ac_load), .IR_LOAD(control_unit_1_ir_load),
    .OUTR_LOAD(control_unit_1_outr_load), .DR_LOAD(control_unit_1_dr_load), .MEM_LOAD(control_unit_1_mem_load));  // open: ADDRESS_OF_INSTRUCTION, PC_TO_AR, M_AR__TO_IR, DECODE, AC_INC, AC_CLR
  adder_circ adder_circ_1 (
    .DR(register_4_q), .AC(counter_2_q), .D0(control_unit_1_d0), .T5(control_unit_1_t5),
    .D1(control_unit_1_d1), .D2(control_unit_1_d2), .P(control_unit_1_p), .B11(control_unit_1_b11),
    .R(control_unit_1_r), .B9(control_unit_1_b9), .B7(control_unit_1_b7), .B6(control_unit_1_b6),
    .B5(control_unit_1_b5), .AC_INC(adder_circ_1_ac_inc), .AC_CLR(adder_circ_1_ac_clr), .E(adder_circ_1_e),
    .CLK(not_1_out), .AC_RES(adder_circ_1_ac_res), .INPR(register_1_q));
  not not_1 (not_1_out, clock_1_out);
  D_Flip_Flop E_FLIP_FLOP (.clk(clock_1_out), .D(adder_circ_1_e));  // open: Q, Qn, preset, en, reset
  Register #(.width(16)) register_1 (.Q(register_1_q), .clk(clock_1_out));  // open: D, en, clr
  Register #(.width(16)) register_2 (
    .D(multiplexer_1_out), .en(control_unit_1_outr_load), .Q(out_3), .clk(clock_1_out), .clr(in_1));
  Register #(.width(16)) register_3 (
    .D(multiplexer_1_out), .en(control_unit_1_ar_load), .Q(register_3_q), .clk(clock_1_out), .clr(in_1));
  Counter #(.width(16), .max('hffff)) counter_1 (
    .load(control_unit_1_pc_load), .D(multiplexer_1_out), .count(control_unit_1_pc_inc), .Q(counter_1_q),
    .clk(clock_1_out), .clr(in_1));  // open: carry
  Register #(.width(16)) register_4 (
    .D(multiplexer_1_out), .en(control_unit_1_dr_load), .Q(register_4_q), .clk(clock_1_out), .clr(in_1));
  Counter #(.width(16), .max('hffff)) counter_2 (
    .load(control_unit_1_ac_load), .D(adder_circ_1_ac_res), .count(adder_circ_1_ac_inc), .Q(counter_2_q),
    .clk(clock_1_out), .clr(adder_circ_1_ac_clr));  // open: carry
  Register #(.width(16)) register_5 (
    .D(multiplexer_1_out), .en(control_unit_1_ir_load), .Q(register_5_q), .clk(clock_1_out), .clr(in_1));
  Register #(.width(16)) register_6 (.D(multiplexer_1_out), .en(1'b0), .Q(register_6_q), .clk(clock_1_out), .clr(in_1));
  RAM #(.addrWidth(12), .dataWidth(16), .bus("separate")) ram_1 (
    .addr(register_3_q[11:0]), .din(multiplexer_1_out), .data(ram_1_data), .str(control_unit_1_mem_load),
    .clk(clock_1_out), .ld(control_unit_1_mem_bus));  // open: sel, clr
  Clock clock_1 (.out(clock_1_out));
  Multiplexer #(.select(3), .width(16)) multiplexer_1 (
    .in1(register_3_q), .in2(counter_1_q), .in3(register_4_q), .in4(counter_2_q), .in5(register_5_q),
    .in6(register_6_q), .in7(ram_1_data), .out(multiplexer_1_out), .sel(control_unit_1_sel_bus));  // open: in0, en

  // Notes on the sheet:
  //   INPUT REGISTER
  //   OUTPUT REGISTER
  //   MEMORY
  //   ADDRESS REGISTER
  //   PROGRAM COUNTER
  //   DATA REGISTER
  //   ACCUMMULATOR
  //   INSTRUCTION REGISTER
  //   TEMPORARY REGISTER
  //   MASTER_CLOCK
  //   LOAD TO THIS FROM BUS
endmodule

// CONT_UNIT
module control_unit (
  input  [15:0] INPUT_INSTR,
  input  INC_SC,
  input  CLK_INPUT,
  output D0,
  output D1,
  output D2,
  output T5,
  output B11,
  output [11:0] ADDRESS_OF_INSTRUCTION,
  output B9,
  output B7,
  output B5,
  output B6,
  output MEM_BUS,
  output [2:0] SEL_BUS,
  output R,
  output P,
  output PC_LOAD,
  output PC_INC,
  output AR_LOAD,
  output PC_TO_AR,
  output M_AR__TO_IR,
  output DECODE,
  output AC_LOAD,
  output AC_INC,
  output AC_CLR,
  output IR_LOAD,
  output OUTR_LOAD,
  output DR_LOAD,
  output MEM_LOAD
);

  wire and_1_out, decoder_1_out3, decoder_1_out4, decoder_1_out6, decoder_1_out7, decoder_1_out8,
       decoder_1_out9, decoder_1_out10, decoder_1_out11, decoder_1_out12, decoder_1_out13, decoder_1_out14,
       decoder_1_out15, decoder_2_out3, decoder_2_out4, decoder_2_out5, decoder_2_out6, decoder_2_out7,
       not_1_out, not_2_out, sc_clr_1_sc_clr;
  wire [3:0] SEQUENCE_COUNTER_q;

  SC_CLR sc_clr_1 (
    .D0(D0), .D1(D1), .D2(D2), .T5(T5), .D3(decoder_2_out3), .D4(decoder_2_out4), .T4(decoder_1_out4), .R(R),
    .P(P), .SC_CLR(sc_clr_1_sc_clr));
  Decoder #(.select(4)) decoder_1 (
    .out0(PC_TO_AR), .out1(M_AR__TO_IR), .out2(DECODE), .out3(decoder_1_out3), .out4(decoder_1_out4),
    .out5(T5), .out6(decoder_1_out6), .out7(decoder_1_out7), .out8(decoder_1_out8), .out9(decoder_1_out9),
    .out10(decoder_1_out10), .out11(decoder_1_out11), .out12(decoder_1_out12), .out13(decoder_1_out13),
    .out14(decoder_1_out14), .out15(decoder_1_out15), .sel(SEQUENCE_COUNTER_q));  // open: en
  Decoder #(.select(3)) decoder_2 (
    .out0(D0), .out1(D1), .out2(D2), .out3(decoder_2_out3), .out4(decoder_2_out4), .out5(decoder_2_out5),
    .out6(decoder_2_out6), .out7(decoder_2_out7), .sel(INPUT_INSTR[14:12]));  // open: en
  Counter #(.width(4), .max('hf)) SEQUENCE_COUNTER (
    .count(INC_SC), .Q(SEQUENCE_COUNTER_q), .clk(CLK_INPUT), .clr(sc_clr_1_sc_clr));  // open: load, D, carry
  not not_1 (not_1_out, INPUT_INSTR[15]);
  and and_1 (and_1_out, INPUT_INSTR[15], decoder_1_out3, not_2_out);
  not not_2 (not_2_out, decoder_2_out7);
  and and_2 (R, decoder_2_out7, not_1_out, decoder_1_out3);
  bus_control bus_control_1 (
    .D0(D0), .D1(D1), .D2(D2), .D3(decoder_2_out3), .D4(decoder_2_out4), .D5(decoder_2_out5),
    .D6(decoder_2_out6), .D7(decoder_2_out7), .T0(PC_TO_AR), .T1(M_AR__TO_IR), .T2(DECODE),
    .T3(decoder_1_out3), .T4(decoder_1_out4), .T5(T5), .I(INPUT_INSTR[15]), .P(P), .B10(INPUT_INSTR[10]),
    .S0(SEL_BUS[0]), .S1(SEL_BUS[1]), .S2(SEL_BUS[2]));
  and and_3 (P, INPUT_INSTR[15], decoder_2_out7, decoder_1_out3);
  PC_conns pc_conns_1 (.T1(M_AR__TO_IR), .T4(decoder_1_out4), .D4(decoder_2_out4), .LOAD_PC(PC_LOAD), .INC_PC(PC_INC));
  AR_conns ar_conns_1 (.D7I_prime_T3(and_1_out), .T2(DECODE), .T0(PC_TO_AR), .AR_LD(AR_LOAD));
  AC_conns ac_conns_1 (
    .D0(D0), .D1(D1), .D2(D2), .T5(T5), .B7(INPUT_INSTR[7]), .B9(INPUT_INSTR[9]), .R(R), .P(P),
    .B5(INPUT_INSTR[5]), .B11(INPUT_INSTR[11]), .LOAD_AC(AC_LOAD), .INC_AC(AC_INC), .CLR_AC(AC_CLR));
  IR_conns ir_conns_1 (.T1(M_AR__TO_IR), .LOAD_IR(IR_LOAD));
  OUTR_conns outr_conns_1 (.P(P), .B10(INPUT_INSTR[11]), .LOAD_OUTR(OUTR_LOAD));
  DR_conns dr_conns_1 (.D0(D0), .D1(D1), .D2(D2), .T4(decoder_1_out4), .DR_LOAD(DR_LOAD));
  mem_conns mem_conns_1 (.D3(decoder_2_out3), .T4(decoder_1_out4), .MEM_LOAD(MEM_LOAD));
  and and_4 (MEM_BUS, SEL_BUS[1], SEL_BUS[0], SEL_BUS[2]);

  assign ADDRESS_OF_INSTRUCTION = INPUT_INSTR[11:0];
  assign B5 = INPUT_INSTR[5];
  assign B6 = INPUT_INSTR[6];
  assign B7 = INPUT_INSTR[7];
  assign B9 = INPUT_INSTR[9];
  assign B11 = INPUT_INSTR[11];

  // Notes on the sheet:
  //   I BIT
  //   ONE OF THE OPCODES
  //   T0
  //   T1
  //   T15
  //   CONTROL CIRCUIT LOGIC
  //   D7I'T3 (r)
  //   D7IT3 (p)
endmodule

// BUS_CONTROL
module bus_control (
  input  D0,
  input  D1,
  input  D2,
  input  D3,
  input  D4,
  input  D5,
  input  D6,
  input  D7,
  input  T0,
  input  T1,
  input  T2,
  input  T3,
  input  T4,
  input  T5,
  input  I,
  input  P,
  input  B10,
  output S0,
  output S1,
  output S2
);

  wire and_1_out, and_2_out, and_3_out, and_4_out, and_5_out, not_1_out, or_1_out, or_2_out, or_3_out;

  or or_1 (or_1_out, D2, D1, D0);
  and and_1 (and_1_out, P, B10);
  not not_1 (not_1_out, D7);
  and and_2 (and_2_out, D4, T4);
  and and_3 (and_3_out, not_1_out, I, T3);
  and and_4 (and_4_out, T4, or_1_out);
  and and_5 (and_5_out, D3, T4);
  or or_2 (or_2_out, T1, and_3_out, and_4_out);
  or or_3 (or_3_out, and_5_out, and_1_out);
  or or_4 (S0, and_2_out, T2, or_2_out);
  or or_5 (S1, T0, or_2_out);
  or or_6 (S2, or_3_out, T2, or_2_out);

  // Notes on the sheet:
  //   X4 PAR (D3T4)
  //   X5
  //   X1
  //   X2
  //   X7
endmodule

// AR
module AR_conns (
  input  D7I_prime_T3,
  input  T2,
  input  T0,
  output AR_LD
);

  or or_1 (AR_LD, D7I_prime_T3, T2, T0);
endmodule

// PC
module PC_conns (
  input  T1,
  input  T4,
  input  D4,
  output LOAD_PC,
  output INC_PC
);

  and and_1 (LOAD_PC, T4, D4);

  assign INC_PC = T1;
endmodule

// DR
module DR_conns (
  input  D0,
  input  D1,
  input  D2,
  input  T4,
  output DR_LOAD
);

  wire or_1_out;

  or or_1 (or_1_out, D0, D1, D2);
  and and_1 (DR_LOAD, or_1_out, T4);
endmodule

// AC
module AC_conns (
  input  D0,
  input  D1,
  input  D2,
  input  T5,
  input  B7,
  input  B9,
  input  R,
  input  P,
  input  B5,
  input  B11,
  output LOAD_AC,
  output INC_AC,
  output CLR_AC
);

  wire and_1_out, and_2_out, and_3_out, or_1_out, or_2_out;

  or or_1 (or_1_out, D0, D1, D2);
  or or_2 (or_2_out, B7, B9);
  and and_1 (and_1_out, or_1_out, T5);
  and and_2 (and_2_out, or_2_out, R);
  and and_3 (and_3_out, P, B11);
  and and_4 (INC_AC, R, B5);
  and and_5 (CLR_AC, R, B11);
  or or_3 (LOAD_AC, and_1_out, and_2_out, and_3_out);
endmodule

// IR
module IR_conns (
  input  T1,
  output LOAD_IR
);


  assign LOAD_IR = T1;
endmodule

// OUTR
module OUTR_conns (
  input  P,
  input  B10,
  output LOAD_OUTR
);

  and and_1 (LOAD_OUTR, P, B10);
endmodule

// ADDER_CIRC
module adder_circ (
  input  [15:0] DR,
  input  [15:0] AC,
  input  [15:0] INPR,
  input  D0,
  input  T5,
  input  D1,
  input  D2,
  input  P,
  input  B11,
  input  R,
  input  B9,
  input  B7,
  input  B6,
  input  B5,
  input  CLK,
  output [15:0] AC_RES,
  output AC_INC,
  output AC_CLR,
  output E
);

  wire GATE_add, GATE_and, GATE_com, GATE_dr, GATE_inpr, GATE_load, GATE_shl, GATE_shr, ST_0_c_i_1,
       ST_1_c_i_1, ST_2_c_i_1, ST_3_c_i_1, ST_4_c_i_1, ST_5_c_i_1, ST_6_c_i_1, ST_7_c_i_1, ST_8_c_i_1,
       ST_9_c_i_1, ST_10_c_i_1, ST_11_c_i_1, ST_12_c_i_1, ST_13_c_i_1, ST_14_c_i_1;

  gate_str GATE (
    .D0(D0), .T5(T5), .D1(D1), .D2(D2), .P(P), .B11(B11), .R(R), .B9(B9), .B7(B7), .B6(B6), .B5(B5),
    .AND(GATE_and), .ADD(GATE_add), .DR(GATE_dr), .LOAD(GATE_load), .INPR(GATE_inpr), .COM(GATE_com),
    .SHR(GATE_shr), .SHL(GATE_shl), .INCREMENT(AC_INC), .CLEAR(AC_CLR));
  adder_stage ST_0 (
    .DR_i(DR[0]), .AC_i(AC[0]), .AND(GATE_and), .ADD(GATE_add), .DR(GATE_dr), .Load(GATE_load),
    .INPR(GATE_inpr), .INPR__bit__i(INPR[0]), .COM(GATE_com), .SHR(GATE_shr), .AC_i_1(AC[1]), .SHL(GATE_shl),
    .AC_i_1_2(AC[15]), .C_i_1(ST_0_c_i_1), .CLK(CLK), .AC_i_2(AC_RES[0]));  // open: Ci
  adder_stage ST_1 (
    .DR_i(DR[1]), .AC_i(AC[1]), .AND(GATE_and), .ADD(GATE_add), .DR(GATE_dr), .Load(GATE_load),
    .INPR(GATE_inpr), .INPR__bit__i(INPR[1]), .COM(GATE_com), .SHR(GATE_shr), .AC_i_1(AC[2]), .SHL(GATE_shl),
    .AC_i_1_2(AC[0]), .Ci(ST_0_c_i_1), .C_i_1(ST_1_c_i_1), .CLK(CLK), .AC_i_2(AC_RES[1]));
  adder_stage ST_2 (
    .DR_i(DR[2]), .AC_i(AC[2]), .AND(GATE_and), .ADD(GATE_add), .DR(GATE_dr), .Load(GATE_load),
    .INPR(GATE_inpr), .INPR__bit__i(INPR[2]), .COM(GATE_com), .SHR(GATE_shr), .AC_i_1(AC[3]), .SHL(GATE_shl),
    .AC_i_1_2(AC[1]), .Ci(ST_1_c_i_1), .C_i_1(ST_2_c_i_1), .CLK(CLK), .AC_i_2(AC_RES[2]));
  adder_stage ST_3 (
    .DR_i(DR[3]), .AC_i(AC[3]), .AND(GATE_and), .ADD(GATE_add), .DR(GATE_dr), .Load(GATE_load),
    .INPR(GATE_inpr), .INPR__bit__i(INPR[3]), .COM(GATE_com), .SHR(GATE_shr), .AC_i_1(AC[4]), .SHL(GATE_shl),
    .AC_i_1_2(AC[2]), .Ci(ST_2_c_i_1), .C_i_1(ST_3_c_i_1), .CLK(CLK), .AC_i_2(AC_RES[3]));
  adder_stage ST_4 (
    .DR_i(DR[4]), .AC_i(AC[4]), .AND(GATE_and), .ADD(GATE_add), .DR(GATE_dr), .Load(GATE_load),
    .INPR(GATE_inpr), .INPR__bit__i(INPR[4]), .COM(GATE_com), .SHR(GATE_shr), .AC_i_1(AC[5]), .SHL(GATE_shl),
    .AC_i_1_2(AC[3]), .Ci(ST_3_c_i_1), .C_i_1(ST_4_c_i_1), .CLK(CLK), .AC_i_2(AC_RES[4]));
  adder_stage ST_5 (
    .DR_i(DR[5]), .AC_i(AC[5]), .AND(GATE_and), .ADD(GATE_add), .DR(GATE_dr), .Load(GATE_load),
    .INPR(GATE_inpr), .INPR__bit__i(INPR[5]), .COM(GATE_com), .SHR(GATE_shr), .AC_i_1(AC[6]), .SHL(GATE_shl),
    .AC_i_1_2(AC[4]), .Ci(ST_4_c_i_1), .C_i_1(ST_5_c_i_1), .CLK(CLK), .AC_i_2(AC_RES[5]));
  adder_stage ST_6 (
    .DR_i(DR[6]), .AC_i(AC[6]), .AND(GATE_and), .ADD(GATE_add), .DR(GATE_dr), .Load(GATE_load),
    .INPR(GATE_inpr), .INPR__bit__i(INPR[6]), .COM(GATE_com), .SHR(GATE_shr), .AC_i_1(AC[7]), .SHL(GATE_shl),
    .AC_i_1_2(AC[5]), .Ci(ST_5_c_i_1), .C_i_1(ST_6_c_i_1), .CLK(CLK), .AC_i_2(AC_RES[6]));
  adder_stage ST_7 (
    .DR_i(DR[7]), .AC_i(AC[7]), .AND(GATE_and), .ADD(GATE_add), .DR(GATE_dr), .Load(GATE_load),
    .INPR(GATE_inpr), .INPR__bit__i(INPR[7]), .COM(GATE_com), .SHR(GATE_shr), .AC_i_1(AC[8]), .SHL(GATE_shl),
    .AC_i_1_2(AC[6]), .Ci(ST_6_c_i_1), .C_i_1(ST_7_c_i_1), .CLK(CLK), .AC_i_2(AC_RES[7]));
  adder_stage ST_8 (
    .DR_i(DR[8]), .AC_i(AC[8]), .AND(GATE_and), .ADD(GATE_add), .DR(GATE_dr), .Load(GATE_load),
    .INPR(GATE_inpr), .INPR__bit__i(INPR[8]), .COM(GATE_com), .SHR(GATE_shr), .AC_i_1(AC[9]), .SHL(GATE_shl),
    .AC_i_1_2(AC[7]), .Ci(ST_7_c_i_1), .C_i_1(ST_8_c_i_1), .CLK(CLK), .AC_i_2(AC_RES[8]));
  adder_stage ST_9 (
    .DR_i(DR[9]), .AC_i(AC[9]), .AND(GATE_and), .ADD(GATE_add), .DR(GATE_dr), .Load(GATE_load),
    .INPR(GATE_inpr), .INPR__bit__i(INPR[9]), .COM(GATE_com), .SHR(GATE_shr), .AC_i_1(AC[10]),
    .SHL(GATE_shl), .AC_i_1_2(AC[8]), .Ci(ST_8_c_i_1), .C_i_1(ST_9_c_i_1), .CLK(CLK), .AC_i_2(AC_RES[9]));
  adder_stage ST_10 (
    .DR_i(DR[10]), .AC_i(AC[10]), .AND(GATE_and), .ADD(GATE_add), .DR(GATE_dr), .Load(GATE_load),
    .INPR(GATE_inpr), .INPR__bit__i(INPR[10]), .COM(GATE_com), .SHR(GATE_shr), .AC_i_1(AC[11]),
    .SHL(GATE_shl), .AC_i_1_2(AC[9]), .Ci(ST_9_c_i_1), .C_i_1(ST_10_c_i_1), .CLK(CLK), .AC_i_2(AC_RES[10]));
  adder_stage ST_11 (
    .DR_i(DR[11]), .AC_i(AC[11]), .AND(GATE_and), .ADD(GATE_add), .DR(GATE_dr), .Load(GATE_load),
    .INPR(GATE_inpr), .INPR__bit__i(INPR[11]), .COM(GATE_com), .SHR(GATE_shr), .AC_i_1(AC[12]),
    .SHL(GATE_shl), .AC_i_1_2(AC[10]), .Ci(ST_10_c_i_1), .C_i_1(ST_11_c_i_1), .CLK(CLK), .AC_i_2(AC_RES[11]));
  adder_stage ST_12 (
    .DR_i(DR[12]), .AC_i(AC[12]), .AND(GATE_and), .ADD(GATE_add), .DR(GATE_dr), .Load(GATE_load),
    .INPR(GATE_inpr), .INPR__bit__i(INPR[12]), .COM(GATE_com), .SHR(GATE_shr), .AC_i_1(AC[13]),
    .SHL(GATE_shl), .AC_i_1_2(AC[11]), .Ci(ST_11_c_i_1), .C_i_1(ST_12_c_i_1), .CLK(CLK), .AC_i_2(AC_RES[12]));
  adder_stage ST_13 (
    .DR_i(DR[13]), .AC_i(AC[13]), .AND(GATE_and), .ADD(GATE_add), .DR(GATE_dr), .Load(GATE_load),
    .INPR(GATE_inpr), .INPR__bit__i(INPR[13]), .COM(GATE_com), .SHR(GATE_shr), .AC_i_1(AC[14]),
    .SHL(GATE_shl), .AC_i_1_2(AC[11]), .Ci(ST_12_c_i_1), .C_i_1(ST_13_c_i_1), .CLK(CLK), .AC_i_2(AC_RES[13]));
  adder_stage ST_14 (
    .DR_i(DR[14]), .AC_i(AC[14]), .AND(GATE_and), .ADD(GATE_add), .DR(GATE_dr), .Load(GATE_load),
    .INPR(INPR[14]), .INPR__bit__i(GATE_inpr), .COM(GATE_com), .SHR(GATE_shr), .AC_i_1(AC[15]),
    .SHL(GATE_shl), .AC_i_1_2(AC[13]), .Ci(ST_13_c_i_1), .C_i_1(ST_14_c_i_1), .CLK(CLK), .AC_i_2(AC_RES[14]));
  adder_stage ST_15 (
    .DR_i(DR[15]), .AC_i(AC[15]), .AND(GATE_and), .ADD(GATE_add), .DR(GATE_dr), .Load(GATE_load),
    .INPR(GATE_inpr), .INPR__bit__i(INPR[15]), .COM(GATE_com), .SHR(GATE_shr), .AC_i_1(AC[0]),
    .SHL(GATE_shl), .AC_i_1_2(AC[14]), .Ci(ST_14_c_i_1), .C_i_1(E), .CLK(CLK), .AC_i_2(AC_RES[15]));
endmodule

// GATE_CONT
module gate_str (
  input  D0,
  input  T5,
  input  D1,
  input  D2,
  input  P,
  input  B11,
  input  R,
  input  B9,
  input  B7,
  input  B6,
  input  B5,
  output AND,
  output ADD,
  output DR,
  output LOAD,
  output INPR,
  output COM,
  output SHR,
  output SHL,
  output INCREMENT,
  output CLEAR
);

  and and_1 (AND, D0, T5);
  and and_2 (ADD, D1, T5);
  and and_3 (DR, D2, T5);
  and and_4 (INPR, P, B11);
  and and_5 (COM, R, B9);
  and and_6 (SHR, R, B7);
  and and_7 (SHL, R, B6);
  and and_8 (INCREMENT, R, B5);
  and and_9 (CLEAR, R, B11);
  or or_1 (LOAD, AND, ADD, DR, INPR, COM, SHR, SHL);

  // Notes on the sheet:
  //   AND
  //   ADD
  //   DR
  //   INPR
  //   COM
  //   SHR
  //   SHL
  //   INC
  //   CLR
  //   LD
endmodule

// ADDER_STAGE
module adder_stage (
  input  DR_i,
  input  AC_i,
  input  AND,
  input  ADD,
  input  DR,
  input  Ci,
  input  Load,
  input  INPR,
  input  INPR__bit__i,
  input  COM,
  input  CLK,
  input  SHR,
  input  AC_i_1,
  input  SHL,
  input  AC_i_1_2,
  output C_i_1,
  output AC_i_2
);

  wire adder_1_out, and_1_out, and_2_out, and_3_out, and_4_out, and_5_out, and_6_out, and_7_out, and_8_out,
       and_9_out, not_1_out, not_2_out, or_1_out;

  Adder #(.width(1)) adder_1 (.a(AC_i), .b(DR_i), .out(adder_1_out), .cin(Ci), .cout(C_i_1));
  not not_1 (not_1_out, AC_i);
  and and_1 (and_1_out, DR_i, AC_i, AND);
  and and_2 (and_2_out, ADD, adder_1_out);
  and and_3 (and_3_out, DR, DR_i);
  and and_4 (and_4_out, INPR, INPR__bit__i);
  and and_5 (and_5_out, COM, not_1_out);
  and and_6 (and_6_out, SHR, AC_i_1);
  and and_7 (and_7_out, SHL, AC_i_1_2);
  or or_1 (or_1_out, and_1_out, and_3_out, and_2_out, and_4_out, and_5_out, and_6_out, and_7_out);
  not not_2 (not_2_out, or_1_out);
  and and_8 (and_8_out, Load, or_1_out);
  and and_9 (and_9_out, not_2_out, Load);
  J_K_Flip_Flop j_k_ff_1 (.J(and_8_out), .clk(CLK), .K(and_9_out), .Q(AC_i_2));  // open: Qn, preset, en, reset

  // Notes on the sheet:
  //   FA
  //   AND
  //   ADD
  //   COM
  //   SHR
  //   SHL
  //   AC(i)
endmodule

// MEM
module mem_conns (
  input  D3,
  input  T4,
  output MEM_LOAD
);

  and and_1 (MEM_LOAD, D3, T4);
endmodule

module SC_CLR (
  input  D0,
  input  D1,
  input  D2,
  input  T5,
  input  D3,
  input  D4,
  input  T4,
  input  R,
  input  P,
  output SC_CLR
);

  wire and_1_out, and_2_out, or_1_out, or_2_out;

  or or_1 (or_1_out, D0, D1, D2);
  or or_2 (or_2_out, D3, D4);
  and and_1 (and_1_out, or_1_out, T5);
  and and_2 (and_2_out, or_2_out, T4);
  or or_3 (SC_CLR, and_1_out, and_2_out, R, P);
endmodule
