// Logisim project control_unit.circ as structural Verilog: 1 circuit, main circuit main
module main (
  input  [15:0] in_1,
  input  CLEAR_SC,
  input  INC_SC,
  input  CLK_INPUT,
  output PC_TO_AR,
  output M_AR__TO_IR,
  output DECODE
);

  wire and_1_out, and_2_out, decoder_1_out3, decoder_1_out4, decoder_1_out5, decoder_1_out6, decoder_1_out7,
       decoder_1_out8, decoder_1_out9, decoder_1_out10, decoder_1_out11, decoder_1_out12, decoder_1_out13,
       decoder_1_out14, decoder_1_out15, decoder_2_out0, decoder_2_out1, decoder_2_out2, decoder_2_out3,
       decoder_2_out4, decoder_2_out5, decoder_2_out6, decoder_2_out7, not_1_out;
  wire [3:0] counter_1_q;

  Counter #(.width(4), .max('hf)) counter_1 (
    .count(INC_SC), .Q(counter_1_q), .clk(CLK_INPUT), .clr(CLEAR_SC));  // open: load, D, carry
  Decoder #(.select(4)) decoder_1 (
    .out0(PC_TO_AR), .out1(M_AR__TO_IR), .out2(DECODE), .out3(decoder_1_out3), .out4(decoder_1_out4),
    .out5(decoder_1_out5), .out6(decoder_1_out6), .out7(decoder_1_out7), .out8(decoder_1_out8),
    .out9(decoder_1_out9), .out10(decoder_1_out10), .out11(decoder_1_out11), .out12(decoder_1_out12),
    .out13(decoder_1_out13), .out14(decoder_1_out14), .out15(decoder_1_out15), .sel(counter_1_q));  // open: en
  Decoder #(.select(3)) decoder_2 (
    .out0(decoder_2_out0), .out1(decoder_2_out1), .out2(decoder_2_out2), .out3(decoder_2_out3),
    .out4(decoder_2_out4), .out5(decoder_2_out5), .out6(decoder_2_out6), .out7(decoder_2_out7),
    .sel(in_1[14:12]));  // open: en
  not not_1 (not_1_out, in_1[15]);
  and and_1 (and_1_out, decoder_2_out7, not_1_out, decoder_1_out3);
  and and_2 (and_2_out, in_1[15], decoder_2_out7, decoder_1_out3);

  // Notes on the sheet:
  //   SEQUENCE COUNTER
  //   INPUT INSTRUCTION
  //   ADDRESS OF INSTRUCTION
  //   ONE OF THE OPCODES
  //   T0
  //   T1
  //   T15
  //   I BIT
  //   D7I'T3 (r)
  //   CONTROL CIRCUIT LOGIC HERE
  //   D7IT3 (p)
endmodule
