// Logisim project sample.circ as structural Verilog: 1 circuit, main circuit main
module main (
  input  [15:0] in_1,
  input  INC,
  input  CLEAR,
  input  LOAD,
  input  [11:0] in_5,
  input  [1:0] FROM,
  input  [1:0] TO,
  input  in_8,
  input  [11:0] in_9,
  input  in_10,
  input  in_11,
  input  in_12,
  input  in_13,
  output [15:0] out_14,
  output [1:0] out_15,
  output [11:0] out_16
);

  wire clock_1_out, clock_2_out, clock_3_out, clock_4_out, clock_5_out, decoder_1_out0, decoder_1_out1,
       decoder_1_out2, decoder_1_out3;
  wire [1:0] register_2_q, register_3_q, register_4_q, register_5_q;
  wire [11:0] counter_1_q, counter_2_q;

  Counter #(.width(12), .max('hfff)) counter_1 (
    .load(in_8), .D(in_5), .count(in_10), .Q(counter_1_q), .clk(clock_1_out));  // open: carry, clr
  Clock clock_1 (.out(clock_1_out));
  Counter #(.width(12), .max('hfff)) counter_2 (
    .load(in_8), .D(counter_1_q), .count(in_10), .Q(counter_2_q), .clk(clock_1_out));  // open: carry, clr
  Clock clock_2 (.out(clock_2_out));
  Register register_1 ();  // open: D, en, Q, clk, clr
  Register #(.width(2)) register_2 (.D(out_15), .en(decoder_1_out0), .Q(register_2_q), .clk(clock_2_out));  // open: clr
  Register #(.width(2)) register_3 (.D(out_15), .en(decoder_1_out1), .Q(register_3_q), .clk(clock_2_out));  // open: clr
  Register #(.width(2)) register_4 (.D(out_15), .en(decoder_1_out2), .Q(register_4_q), .clk(clock_2_out));  // open: clr
  Register #(.width(2)) register_5 (.D(out_15), .en(decoder_1_out3), .Q(register_5_q), .clk(clock_2_out));  // open: clr
  Counter #(.width(12), .max('hfff)) counter_3 (.clk(clock_3_out));  // open: load, D, count, Q, carry, clr
  Clock clock_3 (.out(clock_3_out));
  Multiplexer #(.select(2), .width(2)) multiplexer_1 (
    .in0(register_2_q), .in1(register_3_q), .in2(register_4_q), .in3(register_5_q), .out(out_15), .sel(FROM));  // open: en
  Decoder #(.select(2)) decoder_1 (
    .out0(decoder_1_out0), .out1(decoder_1_out1), .out2(decoder_1_out2), .out3(decoder_1_out3), .sel(TO));  // open: en
  Counter #(.width(12), .max('hfff)) counter_4 (
    .load(in_11), .D(in_9), .count(in_12), .Q(out_16), .clk(clock_4_out), .clr(in_13));  // open: carry
  Clock clock_4 (.out(clock_4_out));
  Counter #(.width(16), .max('hffff)) counter_5 (
    .load(LOAD), .D(in_1), .count(INC), .Q(out_14), .clk(clock_5_out), .clr(CLEAR));  // open: carry
  Clock clock_5 (.out(clock_5_out));
endmodule
